// Logisim project coemips.circ as structural Verilog: 17 circuits, main circuit 16bitalu
module main (
  output [15:0] out_1,
  output [15:0] out_2,
  output [15:0] out_3,
  output [15:0] out_4,
  output [15:0] out_5,
  output [15:0] out_6,
  output [15:0] out_7,
  output [15:0] out_8
);

  wire ALUOpLSB, ALUOpMSB, ALUORShiftSelect, ALUSrcSelect, ALUToReg, branchOpLSB, branchOpMSB, clock_1_out,
       Halt, instructionsplitter_1_unsigned, isABranchOp, JAL, MemRead, MemWrite, PC_1ORAddress, put,
       RegORImm, shamtsrc, subop, WriteEnable;
  wire [2:0] instructionsplitter_1_rs, instructionsplitter_1_rt;
  wire [3:0] opcode, shamt;
  wire [7:0] instructionsplitter_1_immediate, lower8bits_1_lower8, lower8bits_2_lower8, pc_1_pc, pc_1_pc_1;
  wire [15:0] alusrc, bit_extender_1_out, bit_extender_2_out, bit_extender_3_out,
       Display_data_sent_to_display, immediate, multiplexer_3_out, multiplexer_4_out, multiplexer_5_out,
       n16bitalu_1_alu_output, ram_1_data, rom_1_data, rsdata, rtdata, shifter_1_shiftoutput;

  LED led_1 (.in(Halt));
  lower8bits lower8bits_1 (._16(rsdata), .lower8(lower8bits_1_lower8));
  Clock clock_1 (.out(clock_1_out));
  pc pc_1 (
    .register(lower8bits_1_lower8), .immediate(instructionsplitter_1_immediate), .sourceregof16b(rsdata),
    .halt(Halt), .CLK(clock_1_out), .bropMSB(branchOpMSB), .bropLSB(branchOpLSB),
    .registerORimmediate(RegORImm), .plusoneORaddress(PC_1ORAddress), .isabranchop(isABranchOp),
    .PC_1(pc_1_pc_1), .PC(pc_1_pc));
  instructiondecoder instructiondecoder_1 (
    .opcode(opcode), .subop(subop), .alusrcselect(ALUSrcSelect), .aluopselectmsb(ALUOpMSB),
    .aluopselectlsb(ALUOpLSB), .aluORshiftSel(ALUORShiftSelect), .put(put), .halt(Halt),
    .writeenable(WriteEnable), .alutoreg(ALUToReg), .memwrite(MemWrite), .memread(MemRead), .jal(JAL),
    .regORimm(RegORImm), .pc_1ORaddress(PC_1ORAddress), .isabranchop(isABranchOp), .branchopmsb(branchOpMSB),
    .branchoplsb(branchOpLSB), .shamtsrc(shamtsrc));
  instructionsplitter instructionsplitter_1 (
    .instruction(rom_1_data), .rt(instructionsplitter_1_rt), .subop(subop), .shamt(shamt),
    .immediate(instructionsplitter_1_immediate), .\unsigned (instructionsplitter_1_unsigned),
    .rs(instructionsplitter_1_rs), .opcode(opcode));
  ROM #(.dataWidth(16)) rom_1 (.addr(pc_1_pc), .data(rom_1_data), .sel(1'b1));
  assign bit_extender_1_out = {{8{instructionsplitter_1_immediate[7]}}, instructionsplitter_1_immediate};  // Bit_Extender bit_extender_1
  assign bit_extender_2_out = {{8{1'b0}}, instructionsplitter_1_immediate};  // Bit_Extender bit_extender_2
  assign bit_extender_3_out = {{8{1'b0}}, pc_1_pc_1};  // Bit_Extender bit_extender_3
  registerfile registerfile_1 (
    .Write_Data(multiplexer_4_out), .Write_Enable(WriteEnable), .Read_Register_1(instructionsplitter_1_rt),
    .Read_Data_1(rtdata), .Read_Data_2(rsdata), .Read_Register_2(instructionsplitter_1_rs),
    .Write_Register(instructionsplitter_1_rs), .CLK(clock_1_out), .r7(out_1), .r6(out_3), .r5(out_5),
    .r4(out_7), .r3(out_2), .r2(out_4), .r1(out_6), .r0(out_8));
  Multiplexer #(.width(16), .disabled(0), .enable("false")) multiplexer_1 (
    .in0(bit_extender_1_out), .in1(bit_extender_2_out), .out(immediate), .sel(instructionsplitter_1_unsigned));
  Multiplexer #(.width(16), .disabled(0), .enable("false")) multiplexer_2 (
    .in0(rtdata), .in1(immediate), .out(alusrc), .sel(ALUSrcSelect));
  _16bitalu u_16bitalu_1 (
    .operand_1(rsdata), .operand_2(alusrc), .OPLSB(ALUOpLSB), .OPMSB(ALUOpMSB),
    .alu_output(n16bitalu_1_alu_output));  // open: c_in, zero_detect
  Multiplexer #(.width(16), .disabled(0), .enable("false")) multiplexer_3 (
    .in0(n16bitalu_1_alu_output), .in1(shifter_1_shiftoutput), .out(multiplexer_3_out), .sel(ALUORShiftSelect));
  shifter shifter_1 (
    .shiftoperand(rsdata), ._4bimm(shamt), .lower4bofreg(rtdata), .shamtsrc(shamtsrc), .subop(subop),
    .shiftoutput(shifter_1_shiftoutput));
  lower8bits lower8bits_2 (._16(rtdata), .lower8(lower8bits_2_lower8));
  RAM #(.dataWidth(16), .bus("separate")) ram_1 (
    .addr(lower8bits_2_lower8), .din(rsdata), .data(ram_1_data), .str(MemWrite), .sel(1'b1),
    .clk(clock_1_out), .ld(MemRead), .clr(1'b0));
  Hex_Digit_Display hex_digit_display_1 (.value(Display_data_sent_to_display[15:12]));  // open: dp
  Hex_Digit_Display hex_digit_display_2 (.value(Display_data_sent_to_display[7:4]));  // open: dp
  Hex_Digit_Display hex_digit_display_3 (.value(Display_data_sent_to_display[11:8]));  // open: dp
  Multiplexer #(.width(16), .disabled(0), .enable("false")) multiplexer_4 (
    .in0(multiplexer_5_out), .in1(bit_extender_3_out), .out(multiplexer_4_out), .sel(JAL));
  Multiplexer #(.width(16), .enable("false")) multiplexer_5 (
    .in0(ram_1_data), .in1(multiplexer_3_out), .out(multiplexer_5_out), .sel(ALUToReg));
  Hex_Digit_Display hex_digit_display_4 (.value(Display_data_sent_to_display[3:0]));  // open: dp
  displayunit Display (
    .data_to_display(rsdata), .put(put), .CLK(clock_1_out),
    .data_sent_to_display(Display_data_sent_to_display));

  // Other names for the same wires on the sheet: r0[15:0] = out_8; r1[15:0] = out_6; r2[15:0] = out_4;
  //   r3[15:0] = out_2; r4[15:0] = out_7; r5[15:0] = out_5; r6[15:0] = out_3; r7[15:0] = out_1

  // Notes on the sheet:
  //   contents of rom_1 (hex, n*v repeats v):
  //   1 241 6001 1001 241 200 12f6 b202 10ff 6000 f000 10ff a009 8009 7000
  //   Navdeep Handa
  //   nkh15@pitt.edu
endmodule

module _16bitalu (
  input  c_in,
  input  OPLSB,
  input  OPMSB,
  input  [15:0] operand_1,
  input  [15:0] operand_2,
  output zero_detect,
  output [15:0] alu_output
);

  wire or_1_out;
  wire [15:0] adder_1_out, and_1_out, nor_1_out, subtractor_1_out;

  Adder #(.width(16)) adder_1 (.a(operand_1), .b(operand_2), .out(adder_1_out), .cin(c_in));  // open: cout
  Subtractor #(.width(16)) subtractor_1 (
    .a(operand_1), .b(operand_2), .out(subtractor_1_out), .bin(c_in));  // open: bout
  assign nor_1_out = ~(operand_1 | operand_2);  // NOR_Gate nor_1, 16 bits wide
  assign and_1_out = operand_1 & operand_2;  // AND_Gate and_1, 16 bits wide
  Multiplexer #(.select(2), .width(16), .disabled(0), .enable("false")) multiplexer_1 (
    .in0(adder_1_out), .in1(subtractor_1_out), .in2(nor_1_out), .in3(and_1_out), .out(alu_output),
    .sel({OPMSB, OPLSB}));
  or or_1 (or_1_out, alu_output[0], alu_output[1], alu_output[2], alu_output[3], alu_output[4], alu_output[5], alu_output[6], alu_output[7], alu_output[8], alu_output[9], alu_output[10], alu_output[11], alu_output[12], alu_output[13], alu_output[14], alu_output[15]);
  not not_1 (zero_detect, or_1_out);
endmodule

module registerfile (
  input  [2:0] Read_Register_1,
  input  [15:0] Write_Data,
  input  Write_Enable,
  input  [2:0] Write_Register,
  input  [2:0] Read_Register_2,
  input  CLK,
  output [15:0] r2,
  output [15:0] r1,
  output [15:0] Read_Data_1,
  output [15:0] r0,
  output [15:0] r7,
  output [15:0] r6,
  output [15:0] r5,
  output [15:0] r4,
  output [15:0] Read_Data_2,
  output [15:0] r3
);

  wire decoder_1_out0, decoder_1_out1, decoder_1_out2, decoder_1_out3, decoder_1_out4, decoder_1_out5,
       decoder_1_out6, decoder_1_out7;

  Decoder #(.select(3), .disabled(0)) decoder_1 (
    .out0(decoder_1_out0), .out1(decoder_1_out1), .out2(decoder_1_out2), .out3(decoder_1_out3),
    .out4(decoder_1_out4), .out5(decoder_1_out5), .out6(decoder_1_out6), .out7(decoder_1_out7),
    .sel(Write_Register), .en(Write_Enable));
  Register #(.width(16)) Reg_000 (.D(Write_Data), .en(decoder_1_out0), .Q(r0), .clk(CLK), .clr(1'b0));
  Register #(.width(16)) Reg_001 (.D(Write_Data), .en(decoder_1_out1), .Q(r1), .clk(CLK), .clr(1'b0));
  Register #(.width(16)) Reg_010 (.D(Write_Data), .en(decoder_1_out2), .Q(r2), .clk(CLK), .clr(1'b0));
  Register #(.width(16)) Reg_011 (.D(Write_Data), .en(decoder_1_out3), .Q(r3), .clk(CLK), .clr(1'b0));
  Register #(.width(16)) Reg_100 (.D(Write_Data), .en(decoder_1_out4), .Q(r4), .clk(CLK), .clr(1'b0));
  Register #(.width(16)) Reg_101 (.D(Write_Data), .en(decoder_1_out5), .Q(r5), .clk(CLK), .clr(1'b0));
  Register #(.width(16)) Reg_110 (.D(Write_Data), .en(decoder_1_out6), .Q(r6), .clk(CLK), .clr(1'b0));
  Register #(.width(16)) Reg_111 (.D(Write_Data), .en(decoder_1_out7), .Q(r7), .clk(CLK), .clr(1'b0));
  Multiplexer #(.select(3), .width(16), .enable("false")) multiplexer_1 (
    .in0(r0), .in1(r1), .in2(r2), .in3(r3), .in4(r4), .in5(r5), .in6(r6), .in7(r7), .out(Read_Data_1),
    .sel(Read_Register_1));
  Multiplexer #(.select(3), .width(16), .enable("false")) multiplexer_2 (
    .in0(r0), .in1(r1), .in2(r2), .in3(r3), .in4(r4), .in5(r5), .in6(r6), .in7(r7), .out(Read_Data_2),
    .sel(Read_Register_2));
endmodule

module pc (
  input  bropMSB,
  input  registerORimmediate,
  input  bropLSB,
  input  [7:0] register,
  input  [7:0] immediate,
  input  plusoneORaddress,
  input  [15:0] sourceregof16b,
  input  halt,
  input  isabranchop,
  input  CLK,
  output [7:0] PC_1,
  output [7:0] PC
);

  wire not_1_out;
  wire [7:0] branchcomparison_1_targetaddress, multiplexer_1_out, multiplexer_2_out, multiplexer_3_out;

  branchcomparison branchcomparison_1 (
    .rs(sourceregof16b), .pc_1(PC_1), .imm(immediate), .opMSB(bropMSB), .opLSB(bropLSB),
    .targetaddress(branchcomparison_1_targetaddress));  // open: Zero
  Multiplexer #(.width(8), .disabled(0), .enable("false")) multiplexer_1 (
    .in0(multiplexer_3_out), .in1(branchcomparison_1_targetaddress), .out(multiplexer_1_out),
    .sel(isabranchop));
  Multiplexer #(.width(8), .disabled(0), .enable("false")) multiplexer_2 (
    .in0(register), .in1(immediate), .out(multiplexer_2_out), .sel(registerORimmediate));
  Register programcounter (.D(multiplexer_1_out), .en(not_1_out), .Q(PC), .clk(CLK), .clr(1'b0));
  not not_1 (not_1_out, halt);
  Multiplexer #(.width(8), .disabled(0), .enable("false")) multiplexer_3 (
    .in0(multiplexer_2_out), .in1(PC_1), .out(multiplexer_3_out), .sel(plusoneORaddress));
  Adder adder_1 (.a(PC), .b(8'h1), .out(PC_1));  // open: cin, cout
endmodule

module displayunit (
  input  [15:0] data_to_display,
  input  put,
  input  CLK,
  output [15:0] data_sent_to_display
);

  Register #(.width(16)) source_reg (.D(data_to_display), .en(put), .Q(data_sent_to_display), .clk(CLK), .clr(1'b0));
endmodule

module instructiondecoder (
  input  [3:0] opcode,
  input  subop,
  output alusrcselect,
  output aluopselectmsb,
  output aluopselectlsb,
  output aluORshiftSel,
  output put,
  output halt,
  output writeenable,
  output alutoreg,
  output memwrite,
  output memread,
  output jal,
  output regORimm,
  output pc_1ORaddress,
  output isabranchop,
  output branchopmsb,
  output branchoplsb,
  output shamtsrc
);

  ALUControls alucontrols_1 (
    .OP3(opcode[3]), .OP2(opcode[2]), .OP1(opcode[1]), .OP0(opcode[0]), .SUBOP(subop),
    .ALUSrcSelect(alusrcselect), .ALUOpSelectMSB(aluopselectmsb), .ALUOpSelectLSB(aluopselectlsb),
    .ALUOrShiftSel(aluORshiftSel));
  PutandHalt putandhalt_1 (.OP3(opcode[3]), .OP2(opcode[2]), .OP1(opcode[1]), .OP0(opcode[0]), .Put(put), .Halt(halt));
  WritesAndALUtoReg writesandalutoreg_1 (
    .OP3(opcode[3]), .OP2(opcode[2]), .OP1(opcode[1]), .OP0(opcode[0]), .SUBOP(subop),
    .WriteEnable(writeenable), .ALUtoReg(alutoreg), .MemWrite(memwrite), .MemRead(memread));
  JAL jal_1 (.OP3(opcode[3]), .OP2(opcode[2]), .OP1(opcode[1]), .JAL(jal));
  branchcontrolsandsomePC branchcontrolsandsomepc_1 (
    .OP3(opcode[3]), .OP2(opcode[2]), .OP1(opcode[1]), .OP0(opcode[0]), .regORimm(regORimm),
    .PCplusOneORAddress(pc_1ORaddress), .isABranchOp(isabranchop), .branchOpMSB(branchopmsb),
    .branchOPLSB(branchoplsb));
  shamtSrc shamtsrc_1 (.OP0(opcode[0]), .shamtSrc(shamtsrc));

  // Other names for the same wires on the sheet: OP0 = opcode[0]; OP1 = opcode[1]; OP2 = opcode[2]; OP3 = opcode[3]
endmodule

module zeroextend (
  input  [7:0] _8_bit_in,
  output [15:0] _16_bit_out
);


  assign _16_bit_out = {{8{1'b0}}, _8_bit_in};
endmodule

module instructionsplitter (
  input  [15:0] instruction,
  output [2:0] rt,
  output subop,
  output [3:0] shamt,
  output [7:0] immediate,
  output \unsigned ,
  output [2:0] rs,
  output [3:0] opcode
);


  assign immediate = instruction[7:0];
  assign opcode = instruction[15:12];
  assign rs = instruction[11:9];
  assign rt = instruction[8:6];
  assign shamt = instruction[4:1];
  assign subop = instruction[0];
  assign \unsigned  = instruction[8];
endmodule

module lower8bits (
  input  [15:0] _16,
  output [7:0] lower8
);


  assign lower8 = _16[7:0];
endmodule

module shifter (
  input  [15:0] shiftoperand,
  input  shamtsrc,
  input  [15:0] lower4bofreg,
  input  subop,
  input  [3:0] _4bimm,
  output [15:0] shiftoutput
);

  wire [3:0] multiplexer_1_out;
  wire [15:0] shifter_1_out, shifter_2_out;

  Multiplexer #(.width(4), .disabled(0), .enable("false")) multiplexer_1 (
    .in0(lower4bofreg[3:0]), .in1(_4bimm), .out(multiplexer_1_out), .sel(shamtsrc));
  Shifter #(.width(16)) shifter_1 (.in(shiftoperand), .\dist (multiplexer_1_out), .out(shifter_1_out));
  Shifter #(.width(16), .shift("lr")) shifter_2 (.in(shiftoperand), .\dist (multiplexer_1_out), .out(shifter_2_out));
  Multiplexer #(.width(16), .disabled(0), .enable("false")) multiplexer_2 (
    .in0(shifter_1_out), .in1(shifter_2_out), .out(shiftoutput), .sel(subop));
endmodule

module branchcomparison (
  input  [15:0] rs,
  input  opMSB,
  input  opLSB,
  input  [7:0] pc_1,
  input  [7:0] imm,
  output Zero,
  output [7:0] targetaddress
);

  wire not_2_out, not_3_out, or_1_out;
  wire [7:0] multiplexer_1_out, multiplexer_2_out, multiplexer_3_out, multiplexer_4_out;

  or or_1 (or_1_out, rs[0], rs[1], rs[2], rs[3], rs[4], rs[5], rs[6], rs[7], rs[8], rs[9], rs[10], rs[11], rs[12], rs[13], rs[14], rs[15]);
  not not_1 (Zero, or_1_out);
  not not_2 (not_2_out, Zero);
  not not_3 (not_3_out, rs[15]);
  Multiplexer #(.width(8), .disabled(0), .enable("false")) multiplexer_1 (
    .in0(pc_1), .in1(imm), .out(multiplexer_1_out), .sel(Zero));
  Multiplexer #(.width(8), .disabled(0), .enable("false")) multiplexer_2 (
    .in0(pc_1), .in1(imm), .out(multiplexer_2_out), .sel(not_2_out));
  Multiplexer #(.width(8), .disabled(0), .enable("false")) multiplexer_3 (
    .in0(pc_1), .in1(imm), .out(multiplexer_3_out), .sel(not_3_out));
  Multiplexer #(.width(8), .disabled(0), .enable("false")) multiplexer_4 (
    .in0(pc_1), .in1(imm), .out(multiplexer_4_out), .sel(rs[15]));
  Multiplexer #(.select(2), .width(8), .enable("false")) multiplexer_5 (
    .in0(multiplexer_1_out), .in1(multiplexer_2_out), .in2(multiplexer_3_out), .in3(multiplexer_4_out),
    .out(targetaddress), .sel({opMSB, opLSB}));
endmodule

module ALUControls (
  input  OP3,
  input  OP2,
  input  OP1,
  input  OP0,
  input  SUBOP,
  output ALUSrcSelect,
  output ALUOpSelectMSB,
  output ALUOpSelectLSB,
  output ALUOrShiftSel
);

  wire and_1_out, and_2_out, and_3_out, not_1_out, not_2_out;

  not not_1 (not_1_out, OP1);
  not not_2 (not_2_out, OP0);
  and and_1 (and_1_out, not_1_out, OP0);
  and and_2 (and_2_out, not_2_out, SUBOP);
  and and_3 (and_3_out, OP1, SUBOP);
  or or_1 (ALUSrcSelect, and_1_out, OP3);
  or or_2 (ALUOpSelectLSB, and_2_out, and_3_out);

  assign ALUOpSelectMSB = OP1;
  assign ALUOrShiftSel = OP2;
endmodule

module PutandHalt (
  input  OP3,
  input  OP2,
  input  OP1,
  input  OP0,
  output Put,
  output Halt
);

  wire not_1_out;

  not not_1 (not_1_out, OP3);
  and and_1 (Put, OP3, OP2, OP1, OP0);
  and and_2 (Halt, not_1_out, OP2, OP1, OP0);
endmodule

module WritesAndALUtoReg (
  input  OP3,
  input  OP2,
  input  OP1,
  input  OP0,
  input  SUBOP,
  output WriteEnable,
  output ALUtoReg,
  output MemWrite,
  output MemRead
);

  wire and_1_out, and_2_out, and_3_out, and_4_out, not_1_out, not_2_out, not_3_out, not_4_out, not_5_out,
       not_6_out, not_7_out, not_8_out, not_9_out, not_10_out, not_11_out, not_12_out, not_13_out,
       not_14_out, not_15_out, not_16_out;

  not not_1 (not_1_out, OP3);
  not not_2 (not_2_out, OP2);
  not not_3 (not_3_out, OP3);
  not not_4 (not_4_out, OP1);
  not not_5 (not_5_out, OP3);
  not not_6 (not_6_out, OP0);
  not not_7 (not_7_out, SUBOP);
  not not_8 (not_8_out, OP1);
  not not_9 (not_9_out, OP0);
  not not_10 (not_10_out, OP2);
  not not_11 (not_11_out, OP1);
  not not_12 (not_12_out, OP3);
  not not_13 (not_13_out, OP0);
  not not_14 (not_14_out, OP3);
  not not_15 (not_15_out, OP0);
  not not_16 (not_16_out, SUBOP);
  and and_1 (and_1_out, not_1_out, not_2_out);
  and and_2 (and_2_out, not_3_out, not_4_out);
  and and_3 (and_3_out, not_5_out, not_6_out, not_7_out);
  and and_4 (and_4_out, OP2, not_8_out, not_9_out);
  or or_1 (ALUtoReg, not_10_out, not_11_out);
  and and_5 (MemWrite, not_12_out, OP2, OP1, not_13_out, SUBOP);
  and and_6 (MemRead, not_14_out, OP2, OP1, not_15_out, not_16_out);
  or or_2 (WriteEnable, and_1_out, and_2_out, and_3_out, and_4_out);
endmodule

module JAL (
  input  OP3,
  input  OP2,
  input  OP1,
  output JAL
);

  wire not_1_out;

  not not_1 (not_1_out, OP1);
  and and_1 (JAL, OP3, OP2, not_1_out);
endmodule

module branchcontrolsandsomePC (
  input  OP3,
  input  OP2,
  input  OP1,
  input  OP0,
  output regORimm,
  output PCplusOneORAddress,
  output isABranchOp,
  output branchOpMSB,
  output branchOPLSB
);

  wire and_1_out, not_2_out, not_3_out;

  not not_1 (regORimm, OP0);
  not not_2 (not_2_out, OP3);
  and and_1 (and_1_out, OP1, OP0);
  not not_3 (not_3_out, OP2);
  or or_1 (PCplusOneORAddress, not_2_out, and_1_out);
  and and_2 (isABranchOp, OP3, not_3_out);

  assign branchOPLSB = OP0;
  assign branchOpMSB = OP1;
endmodule

module shamtSrc (
  input  OP0,
  output shamtSrc
);


  assign shamtSrc = OP0;
endmodule
